// Logisim project alu.circ as structural Verilog: 5 circuits, main circuit Main
module ALU (
  input  [7:0] A,
  input  [7:0] B,
  input  [6:0] opcode,
  output Z,
  output Cmsb,
  output [7:0] Y
);

  wire [7:0] au_1_y, lu_1_y, multiplexer_1_out, multiplexer_2_out, not_1_out, not_2_out;

  assign not_1_out = ~A;  // NOT_Gate not_1, 8 bits wide
  assign not_2_out = ~B;  // NOT_Gate not_2, 8 bits wide
  Multiplexer #(.width(8)) multiplexer_1 (.in0(A), .in1(not_1_out), .out(multiplexer_1_out), .sel(opcode[2]));
  Multiplexer #(.select(2), .width(8)) multiplexer_2 (
    .in0(B), .in1(not_2_out), .in2({8{1'b1}}), .out(multiplexer_2_out), .sel({opcode[0], opcode[1]}));  // open: in3
  AU au_1 (.cin(opcode[3]), .A(multiplexer_1_out), .B(multiplexer_2_out), .Y(au_1_y));  // open: overflow, cout
  LU lu_1 (.A(multiplexer_1_out), .B(multiplexer_2_out), .f2(opcode[4]), .f0(opcode[5]), .Y(lu_1_y));
  Multiplexer #(.width(8)) multiplexer_3 (.in0(au_1_y), .in1(lu_1_y), .out({Cmsb, Y[6:0]}), .sel(opcode[6]));
  nor nor_1 (Z, Y[0], Y[1], Y[2], Y[3], Y[4], Y[5], Y[6], Cmsb);

  assign Y[7] = Cmsb;

  // Notes on the sheet:
  //   Opcode: 
  //   k1: 0000000 | C = A+B
  //   k3: 0001000 | C = A+1
  //   k4: 0000001 | C = A-1
  //   k5: 1100000 | C = AUB
  //   k6: 1000000 | C = AnB
  //   k7: 1110001 | C = !A
  //   k2: 0001010 | C = A+!B+1
endmodule

module AU (
  input  cin,
  input  [7:0] A,
  input  [7:0] B,
  output [7:0] Y,
  output overflow,
  output cout
);

  wire m_full_adder_1_co, m_full_adder_2_co, m_full_adder_3_co, m_full_adder_4_co, m_full_adder_5_co,
       m_full_adder_6_co, m_full_adder_7_co;

  m_full_adder m_full_adder_1 (.cin(cin), .in_2(A[0]), .in_3(B[0]), .s(Y[0]), .co(m_full_adder_1_co));
  m_full_adder m_full_adder_2 (.cin(m_full_adder_1_co), .in_2(A[1]), .in_3(B[1]), .s(Y[1]), .co(m_full_adder_2_co));
  m_full_adder m_full_adder_3 (.cin(m_full_adder_2_co), .in_2(A[2]), .in_3(B[2]), .s(Y[2]), .co(m_full_adder_3_co));
  m_full_adder m_full_adder_4 (.cin(m_full_adder_3_co), .in_2(A[3]), .in_3(B[3]), .s(Y[3]), .co(m_full_adder_4_co));
  m_full_adder m_full_adder_5 (.cin(m_full_adder_4_co), .in_2(A[4]), .in_3(B[4]), .s(Y[4]), .co(m_full_adder_5_co));
  m_full_adder m_full_adder_6 (.cin(m_full_adder_5_co), .in_2(A[5]), .in_3(B[5]), .s(Y[5]), .co(m_full_adder_6_co));
  m_full_adder m_full_adder_7 (.cin(m_full_adder_6_co), .in_2(A[6]), .in_3(B[6]), .s(Y[6]), .co(m_full_adder_7_co));
  m_full_adder m_full_adder_8 (.cin(m_full_adder_7_co), .in_2(A[7]), .in_3(B[7]), .s(Y[7]), .co(cout));
  xor xor_1 (overflow, m_full_adder_7_co, cout);
endmodule

module LU (
  input  [7:0] A,
  input  [7:0] B,
  input  f2,
  input  f0,
  output [7:0] Y
);

  wire [7:0] and_1_out, not_1_out, or_1_out, xor_1_out;

  assign and_1_out = A & B;  // AND_Gate and_1, 8 bits wide
  assign or_1_out = A | B;  // OR_Gate or_1, 8 bits wide
  assign xor_1_out = A ^ B;  // XOR_Gate xor_1, 8 bits wide
  assign not_1_out = ~A;  // NOT_Gate not_1, 8 bits wide
  Multiplexer #(.select(2), .width(8)) multiplexer_1 (
    .in0(and_1_out), .in1(or_1_out), .in2(xor_1_out), .in3(not_1_out), .out(Y), .sel({f2, f0}));
endmodule

module m_full_adder (
  input  cin,
  input  in_2,
  input  in_3,
  output s,
  output co
);

  wire and_1_out, and_2_out, xor_1_out;

  xor xor_1 (xor_1_out, in_2, in_3);
  and and_1 (and_1_out, in_2, in_3);
  xor xor_2 (s, xor_1_out, cin);
  and and_2 (and_2_out, xor_1_out, cin);
  or or_1 (co, and_2_out, and_1_out);
endmodule

module Main (
  input  [7:0] A,
  input  [7:0] B,
  input  [6:0] opcode,
  output [7:0] Y
);

  wire alu_1_cmsb, alu_1_z;

  Hex_Digit_Display hex_digit_display_1 (.value(A[7:4]));  // open: dp
  Hex_Digit_Display hex_digit_display_2 (.value(A[3:0]));  // open: dp
  Hex_Digit_Display hex_digit_display_3 (.value(B[7:4]));  // open: dp
  Hex_Digit_Display hex_digit_display_4 (.value(B[3:0]));  // open: dp
  LED led_1 (.in(alu_1_z));
  ALU alu_1 (.A(A), .B(B), .opcode(opcode), .Z(alu_1_z), .Cmsb(alu_1_cmsb), .Y(Y));
  LED led_2 (.in(alu_1_cmsb));
  Hex_Digit_Display hex_digit_display_5 (.value(Y[7:4]));  // open: dp
  Hex_Digit_Display hex_digit_display_6 (.value(Y[3:0]));  // open: dp

  // Notes on the sheet:
  //   Opcode: 
  //   k1: 0000000 | C = A+B
  //   k2: 0001010 | C = A+!B+1
  //   k3: 0001000 | C = A+1
  //   k4: 0000001 | C = A-1
  //   k5: 1100000 | C = AUB
  //   k6: 1000000 | C = AnB
  //   k7: 1110001 | C = !A
  //   zero flag
  //   C msb
endmodule
