// Logisim project lookahedadder.circ as structural Verilog: 2 circuits, main circuit main
module main (
  input  Cin,
  input  A0,
  input  B0,
  input  A1,
  input  B1,
  input  A2,
  input  B2,
  input  A3,
  input  B3,
  input  A4,
  input  B4,
  input  A5,
  input  B5,
  input  A6,
  input  B6,
  input  A7,
  input  B7
);

  wire and_4_out, and_8_out, and_12_out, and_16_out, and_19_out, and_23_out, and_25_out, and_26_out, C0, C1,
       C2, C3, C4, C5, C6, C7, G0, G1, G2, G3, G4, G5, G6, G7, P0_out, P0Cin, P1_out, P1G0, P1P0Cin, P2_out,
       P2G1, P2P1G0, P2P1P0Cin, P3_out, P3G2, P3P2G1, P3P2P1G0, P3P2P1P0Cin, P4_out, P4G3, P4P3G2, P4P3P2G1,
       P4P3P2P1G0, P4P3P2P1P0Cin, P5_out, P5G4, P5P4G3, P5P4P3G2, P5P4P3P2G1, P5P4P3P2P1G0, P5P4P3P2P1P0Cin,
       P6_out, P6G5, P6P5G4, P6P5P4G3, P6P5P4P3G2, P6P5P4P3P2G1, P6P5P4P3P2P1G0, P6P5P4P3P2P1P0Cin, P7_out,
       S0_s, S1_s, S2_s, S3_s, S4_s, S5_s, S6_s, S7_s;

  and u_G0 (G0, A0, B0);
  xor P0 (P0_out, A0, B0);
  and u_G1 (G1, A1, B1);
  xor P1 (P1_out, A1, B1);
  and u_G2 (G2, A2, B2);
  xor P2 (P2_out, A2, B2);
  and u_G3 (G3, A3, B3);
  xor P3 (P3_out, A3, B3);
  and u_P3G2 (P3G2, P3_out, G2);
  and u_G4 (G4, A4, B4);
  xor P4 (P4_out, A4, B4);
  and and_1 (P4G3, P4_out, G3);
  and u_G5 (G5, A5, B5);
  xor P5 (P5_out, A5, B5);
  and and_2 (P5G4, P5_out, G4);
  and u_G6 (G6, A6, B6);
  xor P6 (P6_out, A6, B6);
  and and_3 (P6G5, P6_out, G5);
  and u_G7 (G7, A7, B7);
  xor P7 (P7_out, A7, B7);
  and and_4 (and_4_out, P7_out, G6);
  and u_P1G0 (P1G0, P1_out, G0);
  and u_P2G1 (P2G1, G1, P2_out);
  and u_P3P2G1 (P3P2G1, P3_out, P2G1);
  and and_5 (P4P3G2, P4_out, P3G2);
  and and_6 (P5P4G3, P5_out, P4G3);
  and and_7 (P6P5G4, P6_out, P5G4);
  and and_8 (and_8_out, P7_out, P6G5);
  and u_P2P1G0 (P2P1G0, P1G0, P2_out);
  and u_P3P2P1G0 (P3P2P1G0, P3_out, P2P1G0);
  and and_9 (P4P3P2G1, P4_out, P3P2G1);
  and and_10 (P5P4P3G2, P5_out, P4P3G2);
  and and_11 (P6P5P4G3, P6_out, P5P4G3);
  and and_12 (and_12_out, P7_out, P6P5G4);
  and u_P0Cin (P0Cin, Cin, P0_out);
  and u_P1P0Cin (P1P0Cin, Cin, P0Cin);
  and u_P2P1P0Cin (P2P1P0Cin, P1P0Cin, P2_out);
  and u_P3P2P1P0Cin (P3P2P1P0Cin, P2P1P0Cin, P3_out);
  and and_13 (P4P3P2P1G0, P4_out, P3P2P1G0);
  and and_14 (P5P4P3P2G1, P5_out, P4P3P2G1);
  and and_15 (P6P5P4P3G2, P6_out, P5P4P3G2);
  and and_16 (and_16_out, P7_out, P6P5P4G3);
  or u_C0 (C0, G0, P0Cin);
  or u_C1 (C1, G1, P1P0Cin, P1G0);
  or u_C2 (C2, G2, P2P1P0Cin, P2P1G0, P2G1);
  and and_17 (P5P4P3P2P1G0, P5_out, P4P3P2P1G0);
  and and_18 (P6P5P4P3P2G1, P6_out, P5P4P3P2G1);
  and and_19 (and_19_out, P7_out, P6P5P4P3G2);
  or u_C3 (C3, G3, P3P2P1P0Cin, P3P2P1G0, P3P2G1, P3G2);
  and and_20 (P4P3P2P1P0Cin, P4_out, P3P2P1P0Cin);
  and and_21 (P5P4P3P2P1P0Cin, P5_out, P4P3P2P1P0Cin);
  and and_22 (P6P5P4P3P2P1G0, P6_out, P5P4P3P2P1G0);
  and and_23 (and_23_out, P7_out, P6P5P4P3P2G1);
  m_full_adder S0 (.cin(Cin), .A(A0), .B(B0), .s(S0_s));  // open: co
  m_full_adder S1 (.cin(C0), .A(A1), .B(B1), .s(S1_s));  // open: co
  m_full_adder S2 (.cin(C1), .A(A2), .B(B2), .s(S2_s));  // open: co
  m_full_adder S3 (.cin(C2), .A(A3), .B(B3), .s(S3_s));  // open: co
  m_full_adder S4 (.cin(C3), .A(A4), .B(B4), .s(S4_s));  // open: co
  or or_1 (C4, G4, P4P3P2P1P0Cin, P4P3P2P1G0, P4P3P2G1, P4P3G2, P4G3);
  m_full_adder S5 (.cin(C4), .A(A5), .B(B5), .s(S5_s));  // open: co
  m_full_adder S6 (.cin(C5), .A(A6), .B(B6), .s(S6_s));  // open: co
  m_full_adder S7 (.cin(C6), .A(A7), .B(B7), .s(S7_s));  // open: co
  and and_24 (P6P5P4P3P2P1P0Cin, P6_out, P5P4P3P2P1P0Cin);
  and and_25 (and_25_out, P7_out, P6P5P4P3P2P1G0);
  or or_2 (C5, G5, P5P4P3P2P1P0Cin, P5P4P3P2P1G0, P5P4P3P2G1, P5P4P3G2, P5P4G3, P5G4);
  or or_3 (C6, G6, P6P5P4P3P2P1P0Cin, P6P5P4P3P2P1G0, P6P5P4P3P2G1, P6P5P4P3G2, P6P5P4G3, P6P5G4, P6G5);
  and and_26 (and_26_out, P7_out, P6P5P4P3P2P1P0Cin);
  or or_4 (C7, G7, and_26_out, and_25_out, and_23_out, and_19_out, and_16_out, and_12_out, and_8_out, and_4_out);
  // Probe on S7_s
  // Probe on S6_s
  // Probe on S5_s
  // Probe on S4_s
  // Probe on S3_s
  // Probe on S2_s
  // Probe on S1_s
  // Probe on S0_s
endmodule

module m_full_adder (
  input  cin,
  input  A,
  input  B,
  output s,
  output co
);

  wire and_1_out, and_2_out, xor_1_out;

  xor xor_1 (xor_1_out, A, B);
  and and_1 (and_1_out, A, B);
  xor xor_2 (s, xor_1_out, cin);
  and and_2 (and_2_out, xor_1_out, cin);
  or or_1 (co, and_2_out, and_1_out);
endmodule
